# Fritzing sketch Circuit (saved by Fritzing 0.9.9b)
breadboards: 1

parts:
  Board = Arduino Uno (Rev3) - ICSP
  U1 = Vibration Motor- ROB-08449 [package=vibe-motor-10mm]
  Grove1 = Grove 4 Digit Display
  R1 = Resistor [tolerance=±5% power=0.25 resistance=220 package=THT]
  S1 = Pushbutton [package="[THT]"]
  S3 = Pushbutton [package="[THT]"]
  R3 = Resistor [tolerance=±5% power=0.25 resistance=220 package=THT]
  Switch_5 = Pushbutton [package="[THT]"]
  R5 = Resistor [tolerance=±5% power=0.25 resistance=220 package=THT]

nets:
  5V: Board.5V, Grove1.VCC, S1.Pin_1, S1.Pin_2, S3.Pin_1, S3.Pin_2, Switch_5.Pin_1, Switch_5.Pin_2
  GND: Board.GND, U1.+, Grove1.GND, R1.Pin_1, R3.Pin_1, R5.Pin_1
  N1: Board.D11_PWM/MOSI, Switch_5.Pin_3, Switch_5.Pin_4, R5.Pin_0
  N2: Board.D12/MISO, S3.Pin_3, S3.Pin_4, R3.Pin_0
  N3: Board.D13/SCK, R1.Pin_0, S1.Pin_3, S1.Pin_4
  N4: Board.D2, Grove1.CLK
  N5: Board.D3_PWM, Grove1.DIO
  N6: Board.D7, U1.-
